# Fritzing sketch adapterBoard (saved by Fritzing 0.9.1b)
circuit board: 2.77161cm x 3.3384cm
breadboards: 1

parts:
  DWM1k = Decawave DWM1000 [package="23 mm x 13 mm x 2.9 mm 24- pin side castellation package"]
  18 = male pin header, 9 pins [form="♂ (male)"]
  1 = male pin header, 9 pins [form="♂ (male)"]

nets:
  N1: DWM1k.pin1, 1.pin1
  N2: DWM1k.pin2, 1.pin2
  N3: DWM1k.pin3, 1.pin3
  N4: DWM1k.pin4, 1.pin4
  N5: DWM1k.pin5, DWM1k.pin6, DWM1k.pin7, 1.pin5
  N6: DWM1k.pin8, DWM1k.pin16, DWM1k.pin21, DWM1k.pin23, DWM1k.pin24, 18.pin1
  N7: DWM1k.pin9, 1.pin6
  N8: DWM1k.pin10, 1.pin7
  N9: DWM1k.pin11, 1.pin8
  N10: DWM1k.pin12, 1.pin9
  N11: DWM1k.pin13, 18.pin9
  N12: DWM1k.pin14, 18.pin8
  N13: DWM1k.pin15, 18.pin7
  N14: DWM1k.pin17, 18.pin6
  N15: DWM1k.pin18, 18.pin5
  N16: DWM1k.pin19, 18.pin4
  N17: DWM1k.pin20, 18.pin3
  N18: DWM1k.pin22, 18.pin2

notes:
  DWM1000
  Adapter
  1/10in
  GND
  by umkippen.com

custom parts:
  Decawave DWM1000: A time of flight rf distance sensor module from decawave
