# Fritzing sketch AdapterBoardTestBed (saved by Fritzing 0.9.1b)
breadboards: 1

parts:
  Module1 = Decawave DWM1000 Adapter Board [package="Custom 27.7mm x 33.4mm"]
  Part1 = Arduino Pro Mini v13
  R1 = Resistor [tolerance=±5% resistance=330 package="0805 [SMD]"]

nets:
  N1: Module1.RSTn, Part1.D9_PWM
  VDD: Module1.VDD, Part1.VCC
  N2: Module1.SPICSn, Part1.D10_PWM/SS
  N3: Module1.SPIMOSI, Part1.D11_PWM/MOSI
  N4: Module1.SPIMISO, Part1.D12/MISO
  N5: Module1.SPICLK, Part1.D13/SCK
  N6: Module1.GPIO8_/_IRQ, Part1.D2, R1.Pin_0
  GND: Module1.GND, Part1.GND, R1.Pin_1

custom parts:
  Decawave DWM1000 Adapter Board: Adapter Board 0.1 in for the Decawave DWM1000 UWB RF module
